// Logisim project CU.circ as structural Verilog: 1 circuit, main circuit CU
module CU (
  input  Ext_Reset,
  input  Clk,
  input  [7:0] Flags,
  input  [7:0] Instruction,
  input  Mul_In,
  input  Cin,
  input  JP1,
  input  JP2,
  input  Halt_In,
  input  [7:0] in_10,
  output R0_En,
  output R0_Set,
  output R1_En,
  output R1_Set,
  output R2_En,
  output R2_Set,
  output R3_En,
  output R3_Set,
  output R4_En,
  output R4_Set,
  output R5_En,
  output R5_Set,
  output R6_En,
  output R6_Set,
  output R7_En,
  output R7_Set,
  output ROM_En,
  output RAM_CLK,
  output PC_CLK,
  output Halt,
  output Cout,
  output RAM_L,
  output RAM_H,
  output PC_L,
  output ACC_En,
  output [2:0] Shift,
  output RAM_SET,
  output ACC_Set,
  output RAM_EN,
  output PC_H,
  output Flag_set,
  output Inst_Set,
  output [2:0] ALU,
  output [7:0] out_44
);

  wire ACC_En_t, and_10_out, and_11_out, and_12_out, and_13_out, and_14_out, and_15_out, and_16_out,
       and_17_out, and_18_out, and_19_out, and_20_out, and_21_out, and_22_out, and_23_out, and_24_out,
       and_25_out, and_26_out, and_27_out, and_28_out, and_29_out, and_30_out, and_31_out, and_32_out,
       and_33_out, and_34_out, and_35_out, and_36_out, BRANCH, Clk_t, controlled_buffer_1_out, Decode, En,
       En1, En2, INC, Jump_1, Jump_2, Move, not_1_out, not_2_out, not_3_out, not_4_out, not_5_out, not_6_out,
       not_7_out, not_8_out, not_9_out, not_10_out, not_11_out, not_12_out, not_13_out, not_14_out,
       not_15_out, not_16_out, not_17_out, not_18_out, not_19_out, not_20_out, not_21_out, not_22_out,
       not_23_out, not_24_out, or_1_out, or_2_out, or_3_out, PC_CLK_t, pull_resistor_2_node,
       pull_resistor_12_node, pull_resistor_18_node, pull_resistor_29_node, pull_resistor_38_node,
       pull_resistor_41_node, R0E, R0S, R1E, R1S, R2E, R2S, R3E, R3S, R4E, R4S, R5E, R5S, R6E, R6S, R7E, R7S,
       Reset, Set, stp_1_decode, stp_1_exc1, stp_1_exc2, stp_1_fectch, stp_1_out_3, stp_1_out_4, stp_1_out_5,
       stp_1_pc;
  wire [7:0] register_1_q, register_2_q;

  not not_1 (not_1_out, Halt);
  assign controlled_buffer_1_out = En1 ? En1 : 1'bz;  // Controlled_Buffer controlled_buffer_1
  assign controlled_buffer_1_out = En2 ? En2 : 1'bz;  // Controlled_Buffer controlled_buffer_2
  and and_1 (R0_En, pull_resistor_12_node, R0E, controlled_buffer_1_out);
  and and_2 (R1_En, pull_resistor_12_node, R1E, controlled_buffer_1_out);
  and and_3 (R2_En, pull_resistor_12_node, R2E, controlled_buffer_1_out);
  and and_4 (R3_En, pull_resistor_12_node, R3E, controlled_buffer_1_out);
  and and_5 (R4_En, pull_resistor_12_node, R4E, controlled_buffer_1_out);
  and and_6 (R5_En, pull_resistor_12_node, R5E, controlled_buffer_1_out);
  and and_7 (R6_En, pull_resistor_12_node, R6E, controlled_buffer_1_out);
  and and_8 (R7_En, pull_resistor_12_node, R7E, controlled_buffer_1_out);
  Pull_Resistor pull_resistor_1 (.node(ROM_En));
  Pull_Resistor pull_resistor_2 (.node(pull_resistor_2_node));
  or or_1 (or_1_out, Ext_Reset, pull_resistor_2_node);
  and and_9 (Clk_t, Clk, not_1_out);
  Pull_Resistor pull_resistor_3 (.node(controlled_buffer_1_out));
  Pull_Resistor pull_resistor_4 (.node(R0E));
  Pull_Resistor pull_resistor_5 (.node(R1E));
  Pull_Resistor pull_resistor_6 (.node(R2E));
  Pull_Resistor pull_resistor_7 (.node(R3E));
  Pull_Resistor pull_resistor_8 (.node(R4E));
  Pull_Resistor pull_resistor_9 (.node(R5E));
  Pull_Resistor pull_resistor_10 (.node(R6E));
  Pull_Resistor pull_resistor_11 (.node(R7E));
  Pull_Resistor pull_resistor_12 (.node(pull_resistor_12_node));
  assign pull_resistor_12_node = En ? En : 1'bz;  // Controlled_Buffer controlled_buffer_3
  not not_2 (not_2_out, Instruction[6]);
  not not_3 (not_3_out, Instruction[5]);
  not not_4 (not_4_out, Instruction[6]);
  not not_5 (not_5_out, Instruction[5]);
  not not_6 (not_6_out, Instruction[7]);
  not not_7 (not_7_out, Instruction[5]);
  not not_8 (not_8_out, Instruction[4]);
  not not_9 (not_9_out, Instruction[3]);
  not not_10 (not_10_out, Instruction[4]);
  not not_11 (not_11_out, Instruction[3]);
  not not_12 (not_12_out, Instruction[4]);
  not not_13 (not_13_out, Instruction[7]);
  and and_10 (and_10_out, not_13_out, Instruction[6], Instruction[5]);
  not not_14 (not_14_out, Clk_t);
  not not_15 (not_15_out, Clk_t);
  STP stp_1 (
    .Reset(or_1_out), .CLK(Clk_t), .out_3(stp_1_out_3), .out_4(stp_1_out_4), .out_5(stp_1_out_5),
    .PC(stp_1_pc), .Rst(Reset), .Fectch(stp_1_fectch), .Decode(stp_1_decode), .Exc1(stp_1_exc1),
    .Exc2(stp_1_exc2));
  and and_11 (and_11_out, Instruction[7], not_2_out, not_3_out);
  and and_12 (and_12_out, Instruction[7], not_4_out, not_5_out);
  not not_16 (not_16_out, Instruction[7]);
  not not_17 (not_17_out, Instruction[6]);
  not not_18 (not_18_out, Instruction[5]);
  and and_13 (and_13_out, not_6_out, Instruction[6], not_7_out);
  and and_14 (and_14_out, not_8_out, not_9_out);
  and and_15 (and_15_out, Instruction[4], Instruction[3]);
  and and_16 (and_16_out, En1, Move, not_10_out, not_11_out);
  and and_17 (and_17_out, En1, Move, not_12_out, Instruction[3]);
  and and_18 (and_18_out, BRANCH, not_14_out);
  and and_19 (and_19_out, BRANCH, not_15_out);
  assign pull_resistor_2_node = Reset ? Reset : 1'bz;  // Controlled_Buffer controlled_buffer_4
  Pull_Resistor pull_resistor_13 (.node(Inst_Set));
  assign Inst_Set = stp_1_fectch ? stp_1_fectch : 1'bz;  // Controlled_Buffer controlled_buffer_5
  Pull_Resistor pull_resistor_14 (.node(RAM_CLK));
  Pull_Resistor pull_resistor_15 (.node(RAM_L));
  Pull_Resistor pull_resistor_16 (.node(RAM_H));
  Pull_Resistor pull_resistor_17 (.node(RAM_SET));
  not not_19 (not_19_out, Instruction[1]);
  not not_20 (not_20_out, Instruction[0]);
  not not_21 (not_21_out, Instruction[0]);
  not not_22 (not_22_out, Instruction[2]);
  and and_20 (and_20_out, Decode, and_21_out);
  and and_21 (and_21_out, not_16_out, not_17_out, not_18_out);
  and and_22 (and_22_out, Decode, and_13_out);
  or or_2 (or_2_out, and_14_out, and_15_out);
  Decoder #(.disabled("Z"), .select(3), .tristate("true")) decoder_1 (
    .out0(R0S), .out1(R1S), .out2(R2S), .out3(R3S), .out4(R4S), .out5(R5S), .out6(R6S), .out7(R7S),
    .sel({Instruction[0], Instruction[1], Instruction[2]}), .en(and_16_out));
  Decoder #(.disabled("Z"), .select(3), .tristate("true")) decoder_2 (
    .out0(R0E), .out1(R1E), .out2(R2E), .out3(R3E), .out4(R4E), .out5(R5E), .out6(R6E), .out7(R7E),
    .sel({Instruction[0], Instruction[1], Instruction[2]}), .en(and_17_out));
  S_R_Flip_Flop #(.trigger("high")) s_r_ff_1 (
    .S(and_23_out), .R(pull_resistor_18_node), .clk(Clk_t), .Q(BRANCH), .reset(Reset));  // open: Qn, preset
  and and_23 (and_23_out, Decode, and_10_out);
  Pull_Resistor pull_resistor_18 (.node(pull_resistor_18_node));
  and and_24 (and_24_out, En1, and_18_out);
  and and_25 (and_25_out, and_18_out, En2);
  and and_26 (and_26_out, Jump_1, and_19_out);
  and and_27 (and_27_out, and_19_out, Jump_2);
  Pull_Resistor pull_resistor_19 (.node(Decode));
  assign Decode = stp_1_decode ? stp_1_decode : 1'bz;  // Controlled_Buffer controlled_buffer_6
  assign ROM_En = Inst_Set ? Inst_Set : 1'bz;  // Controlled_Buffer controlled_buffer_7
  and and_28 (and_28_out, and_11_out, and_29_out);
  and and_29 (and_29_out, Instruction[2], not_19_out, not_20_out);
  and and_30 (and_30_out, not_21_out, Instruction[1], not_22_out);
  S_R_Flip_Flop #(.trigger("high")) s_r_ff_2 (
    .S(and_20_out), .R(PC_CLK), .clk(Clk_t), .Q(Set));  // open: reset, Qn, preset
  Register #(.trigger("high"), .width(3)) alu_reg (.D(Instruction[2:0]), .en(Clk_t), .clk(Set), .Q(ALU), .clr(PC_CLK));
  S_R_Flip_Flop #(.trigger("high")) s_r_ff_3 (
    .S(and_22_out), .R(PC_CLK), .clk(Clk_t), .Q(Move));  // open: reset, Qn, preset
  assign RAM_SET = and_17_out ? and_17_out : 1'bz;  // Controlled_Buffer controlled_buffer_8
  assign ROM_En = and_24_out ? and_24_out : 1'bz;  // Controlled_Buffer controlled_buffer_9
  assign PC_CLK = and_24_out ? and_24_out : 1'bz;  // Controlled_Buffer controlled_buffer_10
  assign ROM_En = and_25_out ? and_25_out : 1'bz;  // Controlled_Buffer controlled_buffer_11
  assign PC_CLK = and_25_out ? and_25_out : 1'bz;  // Controlled_Buffer controlled_buffer_12
  Pull_Resistor pull_resistor_20 (.node(En1));
  assign En1 = stp_1_exc1 ? stp_1_exc1 : 1'bz;  // Controlled_Buffer controlled_buffer_13
  or or_3 (or_3_out, Halt_In, and_28_out);
  and and_31 (and_31_out, and_12_out, and_30_out);
  assign PC_CLK_t = and_31_out ? ~and_31_out : 1'bz;  // Controlled_Inverter controlled_inverter_1
  assign Reset = and_31_out ? ~and_31_out : 1'bz;  // Controlled_Inverter controlled_inverter_2
  Register #(.trigger("high")) register_1 (
    .D(in_10), .en(and_24_out), .clk(and_24_out), .Q(register_1_q));  // open: clr
  Register #(.trigger("high")) register_2 (
    .D(in_10), .en(and_25_out), .clk(and_25_out), .Q(register_2_q));  // open: clr
  Pull_Resistor pull_resistor_21 (.node(PC_CLK));
  Pull_Resistor pull_resistor_22 (.node(PC_L));
  Pull_Resistor pull_resistor_23 (.node(PC_H));
  Register #(.trigger("high"), .width(1)) register_3 (
    .D(or_3_out), .en(or_3_out), .clk(or_3_out), .Q(Halt));  // open: clr
  and and_32 (and_32_out, En1, Move, or_2_out);
  assign out_44 = and_26_out ? register_1_q : 8'bz;  // Controlled_Buffer controlled_buffer_14
  Pull_Resistor pull_resistor_24 (.node(En2));
  assign En2 = stp_1_exc2 ? stp_1_exc2 : 1'bz;  // Controlled_Buffer controlled_buffer_15
  assign ACC_En_t = and_32_out ? and_32_out : 1'bz;  // Controlled_Buffer controlled_buffer_16
  assign out_44 = and_27_out ? register_2_q : 8'bz;  // Controlled_Buffer controlled_buffer_17
  assign PC_L = and_26_out ? and_26_out : 1'bz;  // Controlled_Buffer controlled_buffer_18
  assign PC_H = and_27_out ? and_27_out : 1'bz;  // Controlled_Buffer controlled_buffer_19
  Pull_Resistor pull_resistor_25 (.node(INC));
  assign INC = stp_1_out_3 ? stp_1_out_3 : 1'bz;  // Controlled_Buffer controlled_buffer_20
  Pull_Resistor pull_resistor_26 (.node(Halt));
  not not_23 (not_23_out, Instruction[3]);
  Pull_Resistor pull_resistor_27 (.node(Jump_1));
  assign Jump_1 = stp_1_out_4 ? stp_1_out_4 : 1'bz;  // Controlled_Buffer controlled_buffer_21
  and and_33 (and_33_out, En1, Set);
  and and_34 (and_34_out, En1, Move, Instruction[4], Instruction[3]);
  assign PC_CLK = PC_CLK_t ? PC_CLK_t : 1'bz;  // Controlled_Buffer controlled_buffer_22
  assign ACC_Set = and_33_out ? and_33_out : 1'bz;  // Controlled_Buffer controlled_buffer_23
  and and_35 (and_35_out, En2, Set);
  assign ACC_En = and_35_out ? and_35_out : 1'bz;  // Controlled_Buffer controlled_buffer_24
  assign R0S = and_35_out ? and_35_out : 1'bz;  // Controlled_Buffer controlled_buffer_25
  S_R_Flip_Flop #(.trigger("high")) s_r_ff_4 (
    .S(RAM_SET), .R(PC_CLK), .clk(Clk_t), .Q(RAM_CLK));  // open: reset, Qn, preset
  S_R_Flip_Flop #(.trigger("high")) s_r_ff_5 (
    .S(RAM_EN), .R(PC_CLK), .clk(Clk_t), .Q(RAM_CLK));  // open: reset, Qn, preset
  assign RAM_SET = and_34_out ? and_34_out : 1'bz;  // Controlled_Buffer controlled_buffer_26
  and and_36 (and_36_out, En1, Move, Instruction[4], not_23_out);
  Decoder #(.disabled("Z"), .select(3), .tristate("true")) decoder_3 (
    .out0(R0S), .out1(R1S), .out2(R2S), .out3(R3S), .out4(R4S), .out5(R5S), .out6(R6S), .out7(R7S),
    .sel({Instruction[0], Instruction[1], Instruction[2]}), .en(and_36_out));
  Pull_Resistor pull_resistor_28 (.node(Jump_2));
  assign Jump_2 = stp_1_out_5 ? stp_1_out_5 : 1'bz;  // Controlled_Buffer controlled_buffer_27
  Pull_Resistor pull_resistor_29 (.node(pull_resistor_29_node));
  assign pull_resistor_29_node = En1 ? En1 : 1'bz;  // Controlled_Buffer controlled_buffer_28
  assign pull_resistor_29_node = En2 ? En2 : 1'bz;  // Controlled_Buffer controlled_buffer_29
  Pull_Resistor pull_resistor_30 (.node(R0S));
  Pull_Resistor pull_resistor_31 (.node(R1S));
  Pull_Resistor pull_resistor_32 (.node(R2S));
  Pull_Resistor pull_resistor_33 (.node(R3S));
  Pull_Resistor pull_resistor_34 (.node(R4S));
  Pull_Resistor pull_resistor_35 (.node(R5S));
  Pull_Resistor pull_resistor_36 (.node(R6S));
  Pull_Resistor pull_resistor_37 (.node(R7S));
  Pull_Resistor pull_resistor_38 (.node(pull_resistor_38_node));
  assign pull_resistor_38_node = Set ? Set : 1'bz;  // Controlled_Buffer controlled_buffer_30
  Pull_Resistor pull_resistor_39 (.node(Cout));
  Pull_Resistor pull_resistor_40 (.node(Shift));
  Pull_Resistor pull_resistor_41 (.node(pull_resistor_41_node));
  assign pull_resistor_41_node = stp_1_pc ? stp_1_pc : 1'bz;  // Controlled_Buffer controlled_buffer_31
  not not_24 (not_24_out, BRANCH);
  and and_37 (PC_CLK_t, pull_resistor_41_node, not_24_out);
  and and_38 (R0_Set, pull_resistor_38_node, R0S, pull_resistor_29_node);
  and and_39 (R1_Set, pull_resistor_38_node, R1S, pull_resistor_29_node);
  and and_40 (R2_Set, pull_resistor_38_node, R2S, pull_resistor_29_node);
  and and_41 (R3_Set, pull_resistor_38_node, R3S, pull_resistor_29_node);
  and and_42 (R4_Set, pull_resistor_38_node, R4S, pull_resistor_29_node);
  and and_43 (R5_Set, pull_resistor_38_node, R5S, pull_resistor_29_node);
  and and_44 (R6_Set, pull_resistor_38_node, R6S, pull_resistor_29_node);
  and and_45 (R7_Set, pull_resistor_38_node, R7S, pull_resistor_29_node);
  assign pull_resistor_38_node = Move ? Move : 1'bz;  // Controlled_Buffer controlled_buffer_32
  Pull_Resistor pull_resistor_42 (.node(Flag_set));

  // Other names for the same wires on the sheet: I2 = Instruction[2]; I1 = Instruction[1]; I0 = Instruction[0];
  //   Fetch = Inst_Set; CMP = Flags[4]; Zero = Flags[5]; Cout_t = Flags[6]; Cin_t = Flags[7]; I3 = Instruction[3];
  //   I4 = Instruction[4]; I5 = Instruction[5]; I6 = Instruction[6]; I7 = Instruction[7]; PC_INC = PC_CLK;
  //   RAM_INC = RAM_CLK; Execute = En1; Set1 = En1; Execute_S = En2; Set2 = En2; Set_Flag = Flag_set

  // Notes on the sheet:
  //   MEM
  //   Fetch Logic
  //   ROM >ENABLE
  //   INST-REG > SET
  //   ALU LOGIC
  //   010 XX XXX
  //   HALT Logic    100 XX 100 
  //   NOP LOGIC     100XX101 
  //   ADD A,B  000 XX AAA
  //   BRANCH LOGIC 011 XX ABC 
  //   MOVE ACC to Rx     010 00 Addr
  //   MOVE RX to RAM 010 01 RX
  //   JUMP to Addr: JMP 011 XX 000 
  //   PC_INC
  //   Clk Once
  //   PUSH ACC to Ram 010 11 000
  //   POP Ram to RX    010 10 RX
  //   Flags
endmodule
